// Logisim project HW2_tester_lib.circ as structural Verilog: 3 circuits, main circuit main
module main (
  input  DIRECTION,
  input  in_2
);

  wire c_clock, magic_circuit_terminal_clock, undriven, undriven_2, undriven_3;
  wire [6:0] magic_circuit_terminal;

  magic_circuit magic_circuit (
    .bit_2(undriven), .bit_1(undriven_2), .bit_0(undriven_3), .counter_clock(c_clock),
    .terminal(magic_circuit_terminal), .terminal_clock(magic_circuit_terminal_clock));
  TTY #(.rows(16), .cols(3)) tty_1 (
    .data(magic_circuit_terminal), .clk(magic_circuit_terminal_clock));  // open: we, clr

  // Notes on the sheet:
  //   ENABLE
  //   YOUR CIRCUIT
endmodule

module magic_circuit (
  input  bit_2,
  input  bit_1,
  input  bit_0,
  output counter_clock,
  output [6:0] terminal,
  output terminal_clock
);

  wire [1:0] clock_1_out;

  and and_1 (counter_clock, clock_1_out[1], clock_1_out[0]);
  Clock #(.highDuration(2), .lowDuration(2)) clock_1 (.out(clock_1_out[0]));
  Clock #(.highDuration(4), .lowDuration(4)) clock_2 (.out(clock_1_out[1]));
  binary2ascii binary2ascii_1 (
    .bit_2(bit_2), .bit_1(bit_1), .bit_0(bit_0), .clock_input(clock_1_out), .ascii_output(terminal));
  Clock clock_3 (.out(terminal_clock));

  // Notes on the sheet:
  //   DON'T MODIFY; USE THIS
endmodule

module binary2ascii (
  input  bit_2,
  input  bit_1,
  input  bit_0,
  input  [1:0] clock_input,
  output [6:0] ascii_output
);

  wire [6:0] adder_1_out, adder_2_out, adder_3_out, bit_extender_1_out, bit_extender_2_out,
       bit_extender_3_out;

  assign bit_extender_1_out = {{6{1'b0}}, bit_2};  // Bit_Extender bit_extender_1
  assign bit_extender_2_out = {{6{1'b0}}, bit_1};  // Bit_Extender bit_extender_2
  assign bit_extender_3_out = {{6{1'b0}}, bit_0};  // Bit_Extender bit_extender_3
  Adder #(.width(7)) adder_1 (.a(7'b0110000), .b(bit_extender_1_out), .out(adder_1_out));  // open: cin, cout
  Adder #(.width(7)) adder_2 (.a(7'b0110000), .b(bit_extender_2_out), .out(adder_2_out));  // open: cin, cout
  Adder #(.width(7)) adder_3 (.a(7'b0110000), .b(bit_extender_3_out), .out(adder_3_out));  // open: cin, cout
  Multiplexer #(.select(2), .width(7), .enable("false")) multiplexer_1 (
    .in0(adder_1_out), .in1(adder_2_out), .in2(adder_3_out), .in3(7'b0001010), .out(ascii_output),
    .sel(clock_input));

  // Notes on the sheet:
  //   DON'T TOUCH
endmodule
