// Logisim project analyze_this.circ as structural Verilog: 1 circuit, main circuit what does this do?
module what_does_this_do (
  input  x,
  output y
);

  wire A_q, and_1_out, and_2_out, and_3_out, and_4_out, B_q, clock_1_out, not_1_out, or_1_out, or_2_out,
       xnor_1_out, xor_1_out;

  and and_1 (and_1_out, B_q, A_q);
  xor xor_1 (xor_1_out, A_q, B_q);
  not not_1 (not_1_out, B_q);
  and and_2 (and_2_out, A_q, not_1_out);
  xnor xnor_1 (xnor_1_out, A_q, B_q);
  or or_1 (or_1_out, and_1_out, xor_1_out);
  or or_2 (or_2_out, and_2_out, xnor_1_out);
  and and_3 (and_3_out, x, or_1_out);
  and and_4 (and_4_out, x, or_2_out);
  Clock clock_1 (.out(clock_1_out));
  D_Flip_Flop A (.clk(clock_1_out), .D(and_3_out), .Q(A_q));  // open: Qn, preset, en, reset
  D_Flip_Flop B (.clk(clock_1_out), .D(and_4_out), .Q(B_q));  // open: Qn, preset, en, reset
  and and_5 (y, x, A_q, B_q);
endmodule
