// Logisim project build_counter.circ as structural Verilog: 2 circuits, main circuit todo
module todo (
  input  c,
  output x,
  output y
);

  wire clock_1_out, clock_2_out;
  wire [6:0] _2bits2ascii_ascii_output;

  Clock #(.highDuration(2), .lowDuration(2)) clock_1 (.out(clock_1_out));
  bits2ascii _2bits2ascii (._0_bit(y), ._1_bit(x), .clock_input(clock_1_out), .ascii_output(_2bits2ascii_ascii_output));
  Clock clock_2 (.out(clock_2_out));
  TTY #(.rows(16), .cols(1)) tty_1 (.data(_2bits2ascii_ascii_output), .clk(clock_2_out));  // open: we, clr

  // Notes on the sheet:
  //   ENABLE
  //   half speed
  //   full speed
  //   simple terminal
  //   OUTPUTS
endmodule

module bits2ascii (
  input  _0_bit,
  input  _1_bit,
  input  clock_input,
  output [6:0] ascii_output
);

  wire [6:0] adder_1_out, bit_extender_1_out;

  assign bit_extender_1_out = {{5{1'b0}}, {_1_bit, _0_bit}};  // Bit_Extender bit_extender_1
  Adder #(.width(7)) adder_1 (.a(7'b0110000), .b(bit_extender_1_out), .out(adder_1_out));  // open: cin, cout
  Multiplexer #(.width(7), .enable("false")) multiplexer_1 (
    .in0(7'b0001010), .in1(adder_1_out), .out(ascii_output), .sel(clock_input));
endmodule
