// Logisim project example_combinational_circ.circ as structural Verilog: 6 circuits, main circuit A
module A (
  input  w,
  input  x,
  input  y,
  input  z,
  output A
);

  wire and_1_out, and_2_out;

  and and_1 (and_1_out, x, y);
  and and_2 (and_2_out, x, z);
  or or_1 (A, w, and_1_out, and_2_out);
endmodule

module B (
  input  w,
  input  x,
  input  y,
  input  z,
  output B
);

  wire and_1_out, and_2_out, and_3_out, not_1_out, not_2_out, not_3_out;

  not not_1 (not_1_out, x);
  not not_2 (not_2_out, y);
  not not_3 (not_3_out, z);
  and and_1 (and_1_out, not_1_out, y);
  and and_2 (and_2_out, x, not_2_out, not_3_out);
  and and_3 (and_3_out, not_1_out, z);
  or or_1 (B, and_1_out, and_2_out, and_3_out);
endmodule

module C (
  input  w,
  input  x,
  input  y,
  input  z,
  output C
);

  wire and_1_out, and_2_out, not_1_out, not_2_out;

  not not_1 (not_1_out, y);
  not not_2 (not_2_out, z);
  and and_1 (and_1_out, y, z);
  and and_2 (and_2_out, not_1_out, not_2_out);
  or or_1 (C, and_1_out, and_2_out);
endmodule

module D (
  input  w,
  input  x,
  input  y,
  input  z,
  output D
);

  not not_1 (D, z);
endmodule

module main_with_subcircuits (
  input  w,
  input  x,
  input  y,
  input  z,
  output A,
  output B,
  output C,
  output D
);

  A a_1 (.w(w), .x(x), .y(y), .z(z), .A(A));
  B b_1 (.w(w), .x(x), .y(y), .z(z), .B(B));
  C c_1 (.w(w), .x(x), .y(y), .z(z), .C(C));
  D d_1 (.w(w), .x(x), .y(y), .z(z), .D(D));
endmodule

module main_with_further_simplifications (
  input  w,
  input  x,
  input  y,
  input  z,
  output A,
  output B,
  output C,
  output D
);

  wire and_1_out, and_2_out, and_3_out, and_4_out, not_2_out, not_3_out, or_1_out;

  not not_1 (D, z);
  and and_1 (and_1_out, z, y);
  or or_1 (or_1_out, z, y);
  not not_2 (not_2_out, x);
  not not_3 (not_3_out, or_1_out);
  or or_2 (C, and_1_out, not_3_out);
  and and_2 (and_2_out, not_3_out, x);
  and and_3 (and_3_out, or_1_out, not_2_out);
  and and_4 (and_4_out, or_1_out, x);
  or or_3 (B, and_2_out, and_3_out);
  or or_4 (A, and_4_out, w);

  // Notes on the sheet:
  //   A = z'
  //   Here's an example of how the circuit could be built with less gates.
  //   B = yx + y'z'               = yz + (y + z)'
  //   C = x'y + x'z + xy'z'   = x'(y + z) + b(y + z)'
  //   D = w + xy + xz          = w +x(y + z)
  //   This type of simplication relaxes the minimal signal propagation time objective. It is outside the scope of any course offered in the CPSC department and into the domain of software assisted minimization (see textbook).
endmodule
