// Logisim project simple_counter_split.circ as structural Verilog: 4 circuits, main circuit example
module example (
  input  c,
  output x,
  output y
);

  wire clock_1_out, clock_2_out, D_a_a_input, D_b_b_input;
  wire [6:0] _2bits2ascii_ascii_output;

  D_a D_a (.a(x), .b(y), .c(c), .a_input(D_a_a_input));
  D_b D_b (.b(y), .c(c), .b_input(D_b_b_input));
  Clock #(.highDuration(2), .lowDuration(2)) clock_1 (.out(clock_1_out));
  D_Flip_Flop flip_flop_a (.clk(clock_1_out), .D(D_a_a_input), .Q(x));  // open: Qn, preset, en, reset
  D_Flip_Flop flip_flop_b (.clk(clock_1_out), .D(D_b_b_input), .Q(y));  // open: Qn, preset, en, reset
  bits2ascii _2bits2ascii (._0_bit(y), ._1_bit(x), .clock(clock_1_out), .ascii_output(_2bits2ascii_ascii_output));
  Clock clock_2 (.out(clock_2_out));
  TTY #(.rows(16), .cols(1)) tty_1 (.data(_2bits2ascii_ascii_output), .clk(clock_2_out));  // open: we, clr

  // Notes on the sheet:
  //   ENABLE
  //   c
  //   c
  //   boolean fuction for input to flip-flop-a (D_a):   ab' + a'bc + ac'
  //   boolean fuction for input to flip-flop-b (D_b):   b'c + bc'
  //   a
  //   b
  //   half speed
  //   a
  //   b
  //   full speed
  //   simple terminal
  //   OUTPUTS
endmodule

module bits2ascii (
  input  _0_bit,
  input  _1_bit,
  input  clock,
  output [6:0] ascii_output
);

  wire [6:0] adder_1_out, bit_extender_1_out;

  assign bit_extender_1_out = {{5{1'b0}}, {_1_bit, _0_bit}};  // Bit_Extender bit_extender_1
  Adder #(.width(7)) adder_1 (.a(7'b0110000), .b(bit_extender_1_out), .out(adder_1_out));  // open: cin, cout
  Multiplexer #(.width(7), .enable("false")) multiplexer_1 (
    .in0(7'b0001010), .in1(adder_1_out), .out(ascii_output), .sel(clock));
endmodule

module D_a (
  input  a,
  input  b,
  input  c,
  output a_input
);

  wire and_1_out, and_2_out, and_3_out, not_1_out, not_2_out, not_3_out;

  not not_1 (not_1_out, b);
  not not_2 (not_2_out, a);
  not not_3 (not_3_out, c);
  and and_1 (and_1_out, not_1_out, a);
  and and_2 (and_2_out, not_2_out, c, b);
  and and_3 (and_3_out, not_3_out, a);
  or or_1 (a_input, and_1_out, and_2_out, and_3_out);

  // Notes on the sheet:
  //   boolean fuction for input to flip-flop-a (D_a):   ab' + a'bc + ac'
endmodule

module D_b (
  input  b,
  input  c,
  output b_input
);

  wire and_1_out, and_2_out, not_1_out, not_2_out;

  not not_1 (not_1_out, b);
  not not_2 (not_2_out, c);
  buf and_1 (and_1_out, not_1_out);  // AND_Gate
  buf and_2 (and_2_out, not_2_out);  // AND_Gate
  or or_1 (b_input, and_1_out, and_2_out);

  // Notes on the sheet:
  //   boolean fuction for input to flip-flop-b (D_b):   b'c + bc'
endmodule
